// Logisim project Control Logic.circ as structural Verilog: 1 circuit, main circuit main
module main (
  input  [6:0] opcode,
  output clk_en,
  output dmem_rd,
  output dmem_wr,
  output reg_rd,
  output reg_wr,
  output ALU_en,
  output output_en,
  output pc_en,
  output pc_out_en,
  output pc_wr
);

  wire and_1_out;
  wire [4:0] controlled_buffer_1_out;

  and and_1 (and_1_out, opcode[0], opcode[1]);
  assign controlled_buffer_1_out = and_1_out ? opcode[6:2] : 5'bz;  // Controlled_Buffer controlled_buffer_1
  DotMatrix #(.matrixrows(1), .dotshape("circle")) dotmatrix_1 (
    .col0(controlled_buffer_1_out[4]), .col1(controlled_buffer_1_out[3]), .col2(controlled_buffer_1_out[2]),
    .col3(controlled_buffer_1_out[1]), .col4(controlled_buffer_1_out[0]));
  DotMatrix #(.inputtype("row"), .matrixcols(1), .matrixrows(10), .dotshape("circle")) dotmatrix_2 (
    .row0(clk_en), .row1(dmem_rd), .row2(dmem_wr), .row3(reg_rd), .row4(reg_wr), .row5(ALU_en),
    .row6(output_en), .row7(pc_en), .row8(pc_out_en), .row9(pc_wr));
  ROM #(.addrWidth(5), .dataWidth(10)) rom_1 (
    .addr(controlled_buffer_1_out),
    .data({clk_en, dmem_rd, dmem_wr, reg_rd, reg_wr, ALU_en, output_en, pc_en, pc_out_en, pc_wr}));  // open: sel
  Pull_Resistor pull_resistor_1 (.node({clk_en, dmem_rd, dmem_wr, reg_rd, reg_wr, ALU_en, output_en, pc_en, pc_out_en, pc_wr}));

  // Notes on the sheet:
  //   contents of rom_1 (hex, n*v repeats v):
  //   37e 0 0 0 27e 337 0 0 2d6 0 0 27e 27e 7*0 27e 0 0 0 257 27e 0 327
endmodule
