// Logisim project OUTPUTDISPLAY.circ as structural Verilog: 3 circuits, main circuit Output display
module Output_display (
  input  [7:0] in_1
);

  wire dda_1_lsb_2, dda_1_msb_2, dda_1_out_6, dda_1_out_7, dda_2_lsb_2, dda_2_msb_2, dda_2_out_6,
       dda_2_out_7, dda_3_lsb_2, dda_3_msb_2, dda_3_out_6, dda_3_out_7, dda_4_lsb_2, dda_4_msb_2,
       dda_4_out_6, dda_4_out_7, dda_5_lsb_2, dda_5_msb_2, dda_5_out_6, dda_5_out_7, dda_6_lsb_2,
       dda_6_out_6, dda_6_out_7, dda_7_lsb_2, dda_7_msb_2, dda_7_out_6, dda_7_out_7, dda_8_lsb_2,
       dda_8_msb_2, dda_8_out_6, dda_8_out_7, dda_9_lsb_2, dda_9_out_6, dda_9_out_7, dda_10_lsb_2,
       dda_10_out_6, dda_10_out_7, pull_resistor_1_node;
  wire [3:0] dda_11_msb_2, dda_12_msb_2;
  wire [3:1] dda_11_lsb_2;

  DDA dda_1 (
    .LSB(pull_resistor_1_node), .in_2(pull_resistor_1_node), .in_3(pull_resistor_1_node),
    .MSB(pull_resistor_1_node), .LSB_2(dda_1_lsb_2), .out_6(dda_1_out_6), .out_7(dda_1_out_7),
    .MSB_2(dda_1_msb_2));
  Pull_Resistor pull_resistor_1 (.node(pull_resistor_1_node));
  DDA dda_2 (
    .LSB(in_1[6]), .in_2(dda_3_lsb_2), .in_3(dda_3_out_6), .MSB(dda_3_out_7), .LSB_2(dda_2_lsb_2),
    .out_6(dda_2_out_6), .out_7(dda_2_out_7), .MSB_2(dda_2_msb_2));
  DDA dda_3 (
    .LSB(in_1[7]), .in_2(dda_1_lsb_2), .in_3(dda_1_out_6), .MSB(dda_1_out_7), .LSB_2(dda_3_lsb_2),
    .out_6(dda_3_out_6), .out_7(dda_3_out_7), .MSB_2(dda_3_msb_2));
  DDA dda_4 (
    .LSB(in_1[4]), .in_2(dda_5_lsb_2), .in_3(dda_5_out_6), .MSB(dda_5_out_7), .LSB_2(dda_4_lsb_2),
    .out_6(dda_4_out_6), .out_7(dda_4_out_7), .MSB_2(dda_4_msb_2));
  DDA dda_5 (
    .LSB(in_1[5]), .in_2(dda_2_lsb_2), .in_3(dda_2_out_6), .MSB(dda_2_out_7), .LSB_2(dda_5_lsb_2),
    .out_6(dda_5_out_6), .out_7(dda_5_out_7), .MSB_2(dda_5_msb_2));
  DDA dda_6 (
    .LSB(dda_5_msb_2), .in_2(dda_2_msb_2), .in_3(dda_3_msb_2), .MSB(dda_1_msb_2), .LSB_2(dda_6_lsb_2),
    .out_6(dda_6_out_6), .out_7(dda_6_out_7), .MSB_2(dda_12_msb_2[3]));
  DDA dda_7 (
    .LSB(in_1[2]), .in_2(dda_8_lsb_2), .in_3(dda_8_out_6), .MSB(dda_8_out_7), .LSB_2(dda_7_lsb_2),
    .out_6(dda_7_out_6), .out_7(dda_7_out_7), .MSB_2(dda_7_msb_2));
  DDA dda_8 (
    .LSB(in_1[3]), .in_2(dda_4_lsb_2), .in_3(dda_4_out_6), .MSB(dda_4_out_7), .LSB_2(dda_8_lsb_2),
    .out_6(dda_8_out_6), .out_7(dda_8_out_7), .MSB_2(dda_8_msb_2));
  DDA dda_9 (
    .LSB(dda_8_msb_2), .in_2(dda_10_lsb_2), .in_3(dda_10_out_6), .MSB(dda_10_out_7), .LSB_2(dda_9_lsb_2),
    .out_6(dda_9_out_6), .out_7(dda_9_out_7), .MSB_2(dda_12_msb_2[1]));
  DDA dda_10 (
    .LSB(dda_4_msb_2), .in_2(dda_6_lsb_2), .in_3(dda_6_out_6), .MSB(dda_6_out_7), .LSB_2(dda_10_lsb_2),
    .out_6(dda_10_out_6), .out_7(dda_10_out_7), .MSB_2(dda_12_msb_2[2]));
  DDA dda_11 (
    .LSB(in_1[1]), .in_2(dda_7_lsb_2), .in_3(dda_7_out_6), .MSB(dda_7_out_7), .LSB_2(dda_11_lsb_2[1]),
    .out_6(dda_11_lsb_2[2]), .out_7(dda_11_lsb_2[3]), .MSB_2(dda_11_msb_2[0]));
  DDA dda_12 (
    .LSB(dda_7_msb_2), .in_2(dda_9_lsb_2), .in_3(dda_9_out_6), .MSB(dda_9_out_7), .LSB_2(dda_11_msb_2[1]),
    .out_6(dda_11_msb_2[2]), .out_7(dda_11_msb_2[3]), .MSB_2(dda_12_msb_2[0]));
  _7seg_logic_encoder u_7seg_logic_encoder_1 (.Input({dda_11_lsb_2, in_1[0]}));  // open: A, B, C, D, E, F, G
  _7seg_logic_encoder u_7seg_logic_encoder_2 (.Input(dda_11_msb_2));  // open: A, B, C, D, E, F, G
  _7seg_logic_encoder u_7seg_logic_encoder_3 (.Input(dda_12_msb_2));  // open: A, B, C, D, E, F, G
endmodule

module _7seg_logic_encoder (
  input  [3:0] Input,
  output A,
  output B,
  output C,
  output D,
  output E,
  output F,
  output G
);

  wire decoder_1_out0, decoder_1_out1, decoder_1_out2, decoder_1_out3, decoder_1_out4, decoder_1_out5,
       decoder_1_out6, decoder_1_out7, decoder_1_out8, decoder_1_out9;

  Decoder #(.select(4), .enable("false")) decoder_1 (
    .out0(decoder_1_out0), .out1(decoder_1_out1), .out2(decoder_1_out2), .out3(decoder_1_out3),
    .out4(decoder_1_out4), .out5(decoder_1_out5), .out6(decoder_1_out6), .out7(decoder_1_out7),
    .out8(decoder_1_out8), .out9(decoder_1_out9), .sel(Input));  // open: out10, out11, out12, out13, out14, out15
  or u_A (A, decoder_1_out0, decoder_1_out2, decoder_1_out3, decoder_1_out5, decoder_1_out6, decoder_1_out7, decoder_1_out8, decoder_1_out9);
  or u_B (B, decoder_1_out0, decoder_1_out1, decoder_1_out2, decoder_1_out3, decoder_1_out4, decoder_1_out7, decoder_1_out8, decoder_1_out9);
  or u_C (C, decoder_1_out0, decoder_1_out1, decoder_1_out3, decoder_1_out4, decoder_1_out5, decoder_1_out6, decoder_1_out7, decoder_1_out8, decoder_1_out9);
  or u_D (D, decoder_1_out0, decoder_1_out2, decoder_1_out3, decoder_1_out5, decoder_1_out6, decoder_1_out8);
  or u_E (E, decoder_1_out0, decoder_1_out2, decoder_1_out6, decoder_1_out8);
  or u_F (F, decoder_1_out0, decoder_1_out4, decoder_1_out5, decoder_1_out6, decoder_1_out7, decoder_1_out8, decoder_1_out9);
  or u_G (G, decoder_1_out2, decoder_1_out3, decoder_1_out4, decoder_1_out5, decoder_1_out6, decoder_1_out8, decoder_1_out9);
endmodule

module DDA (
  input  LSB,
  input  in_2,
  input  in_3,
  input  MSB,
  output LSB_2,
  output out_6,
  output out_7,
  output MSB_2
);

  wire decoder_1_out0, decoder_1_out1, decoder_1_out2, decoder_1_out3, decoder_1_out4, decoder_1_out5,
       decoder_1_out6, decoder_1_out7, decoder_1_out8, nor_1_out, or_1_out, or_2_out;
  wire [3:0] adder_1_out, multiplexer_1_out, pull_resistor_2_node;
  wire [3:3] pull_resistor_1_node;

  Pull_Resistor pull_resistor_1 (.node(pull_resistor_1_node[3]));
  or or_1 (or_1_out, decoder_1_out0, decoder_1_out1, decoder_1_out2, decoder_1_out3, decoder_1_out4);
  Decoder #(.select(4), .disabled(0), .enable("false")) decoder_1 (
    .out0(decoder_1_out0), .out1(decoder_1_out1), .out2(decoder_1_out2), .out3(decoder_1_out3),
    .out4(decoder_1_out4), .out5(decoder_1_out5), .out6(decoder_1_out6), .out7(decoder_1_out7),
    .out8(decoder_1_out8), .sel({MSB, in_3, in_2, LSB}));  // open: out9, out10, out11, out12, out13, out14, out15
  nor nor_1 (nor_1_out, or_2_out, or_1_out);
  Multiplexer #(.width(4)) multiplexer_1 (
    .in0({MSB, in_3, in_2, LSB}), .in1(adder_1_out), .out(multiplexer_1_out), .sel(or_2_out));  // open: en
  Adder #(.width(4)) adder_1 (
    .a({MSB, in_3, in_2, LSB}), .b({{2{pull_resistor_1_node[3]}}, 2'b11}), .out(adder_1_out));  // open: cin, cout
  Pull_Resistor pull_resistor_2 (.node(pull_resistor_2_node));
  or or_2 (or_2_out, decoder_1_out5, decoder_1_out6, decoder_1_out7, decoder_1_out8);
  Multiplexer #(.width(4)) multiplexer_2 (
    .in0(multiplexer_1_out), .in1(pull_resistor_2_node), .out({MSB_2, out_7, out_6, LSB_2}), .sel(nor_1_out));  // open: en
endmodule
