// Logisim project PC.circ as structural Verilog: 1 circuit, main circuit main
module main (
  input  write_en,
  input  [7:0] INPUT_DESTN,
  input  Count_en,
  input  CLOCK,
  input  CLEAR,
  input  read_en,
  output [7:0] OUTPUT
);

  wire not_1_out;
  wire [2:0] counter_1_q;
  wire [7:0] adder_1_out, controlled_buffer_1_out, R_q;

  not not_1 (not_1_out, write_en);
  assign controlled_buffer_1_out = write_en ? INPUT_DESTN : 8'bz;  // Controlled_Buffer controlled_buffer_1
  assign controlled_buffer_1_out = not_1_out ? adder_1_out : 8'bz;  // Controlled_Buffer controlled_buffer_2
  Counter #(.width(3), .max('h7)) counter_1 (.Q(counter_1_q), .clk(CLOCK), .clr(CLEAR));  // open: load, D, count, carry
  Counter R (
    .load(Count_en), .D(controlled_buffer_1_out), .count(1'b0), .Q(R_q), .clk(counter_1_q[2]), .clr(CLEAR));  // open: carry
  assign OUTPUT = read_en ? R_q : 8'bz;  // Controlled_Buffer controlled_buffer_3
  Pull_Resistor pull_resistor_1 (.node(OUTPUT));
  Adder adder_1 (.a(R_q), .b(8'h4), .out(adder_1_out));  // open: cin, cout
endmodule
